# Fritzing sketch Schema_Kaffeekanne (saved by Fritzing 1.0.1rc)
breadboards: 1

parts:
  JQ6501 = JQ6500
  SP2 = SPEAKER [package=pcb_mount_speaker]
  0_01_µF1 = Capacitor [package=cap-pth-small2]
  R1 = Resistor [tolerance=±5% resistance=220 power=0.25W package=THT]
  R2 = Resistor [tolerance=±5% resistance=220 power=0.25W package=THT]
  S2 = Toggle Switch [package=THT]
  VCC1 = Battery
  M1 = DOIT Esp32 DevKit v1 (30 pins long, 11 pins width) [part_number=ESP32S-PIN30]
  Power_plug1 = Power plug
  U1 = WS2812 RGB LED strip
  J2 = Basic Servo

nets:
  VCC: JQ6501.RX, 0_01_µF1.2, Power_plug1.VCC, U1.VCC, J2.vcc
  N1: JQ6501.TX, R2.Pin_1
  N2: JQ6501.GND, R1.Pin_1
  N3: JQ6501.DAC_L, SP2.+
  GND: JQ6501.SPK-, 0_01_µF1.1, Power_plug1.GND, U1.GND, J2.gnd
  N4: JQ6501.SPK+, SP2.-
  N5: R1.Pin_0, M1.TX0
  N6: R2.Pin_0, M1.RX0
  N7: S2.L1, VCC1.+
  N8: M1.D2, U1.DIN

notes:
  Kondensator 0,01 F
  Servo]
  Widerstände 670 Ohm
  MP3 Mini Player
  NeoPixel (2)
  Anschlüsse:
  Servo: PIN 2
  NeoPixel: PIN 5
  MP3: RX PIN 17, TX PIN 16

custom parts:
  DOIT Esp32 DevKit v1 (30 pins long, 11 pins width): The DOIT Esp32 DevKit v1 is one of the development board created by DOIT to evaluate the ESP-WROOM-32 module. It is based on the ESP32 microcontroller that boasts Wifi, Bluetooth, Ethernet and Low Power support all in a single chip. (vanepp) made breadboard work, adjusted pin numbering and labels and reduced size of schematic and cleaned up pcb. This chip is 30pins long (2 x15) and 11 pins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
  WS2812 RGB LED strip: WS2812 strip
